# Fritzing sketch schematic (saved by Fritzing 0.7.11b)
stripboards: 1

parts:
  J2 = PCD8544 LCD [form="♂ (male)" package=THT]
  R1 = Resistor [tolerance=±5% resistance=10k package=THT]
  R2 = Resistor [tolerance=±5% resistance=10k package=THT]
  R3 = Resistor [tolerance=±5% resistance=10k package=THT]
  R4 = Resistor [tolerance=±5% resistance=10k package=THT]
  S1 = Pushbutton [package="[THT]"]
  S2 = Pushbutton [package="[THT]"]
  S3 = Pushbutton [package="[THT]"]
  S4 = Pushbutton [package="[THT]"]
  RPi_GPIO2 = RPi GPIO Header [form="♂ (shrouded male)" package=THT]

nets:
  N1: J2.RST, RPi_GPIO2.GPIO_24
  N2: J2.CE, RPi_GPIO2.GPIO_8_(SPI_CS0)
  N3: J2.DC, RPi_GPIO2.GPIO_23
  N4: J2.DIN, RPi_GPIO2.GPIO_10_(SPI_MOSI)
  N5: J2.CLK, RPi_GPIO2.GPIO_11_(SPI_SCLK)
  VCC: J2.VCC, R1.Pin_0, R2.Pin_0, R3.Pin_0, R4.Pin_0, RPi_GPIO2.+3.3V
  N6: J2.LIGHT, RPi_GPIO2.GPIO_18_(PCM_CLK)
  N7: J2.GND, S1.Pin_1, S1.Pin_2, S2.Pin_3, S2.Pin_4, S3.Pin_3, S3.Pin_4, S4.Pin_3, S4.Pin_4, RPi_GPIO2.Ground
  N8: R1.Pin_1, S1.Pin_3, S1.Pin_4, RPi_GPIO2.GPIO_22
  N9: R2.Pin_1, S2.Pin_1, S2.Pin_2, RPi_GPIO2.GPIO_25
  N10: R3.Pin_1, S3.Pin_1, S3.Pin_2, RPi_GPIO2.GPIO_17
  N11: R4.Pin_1, S4.Pin_1, S4.Pin_2, RPi_GPIO2.GPIO_14_(UART_TxD)

notes:
  RPi / PCD8544 header
  (c) Richard Hull 2013

custom parts:
  PCD8544 LCD: generic Nokia 5110 LCD
